# Fritzing sketch arduino-uno-layout (saved by Fritzing 0.9.4)
breadboards: 2

parts:
  LCD1 = LCD screen
  Part1 = Arduino Uno (Rev3)
  HT9032D1 = HT9032D Calle ID Module [part_number="HT9032D Module"]
  Q1 = NPN-Transistor [part_number=2N3904 package="TO92 [THT]"]
  R2 = Resistor [tolerance=±5% resistance=10k package=THT]
  R3 = Resistor [tolerance=±5% resistance=470 package=THT]
  S1 = Round Pushbutton
  R1 = Rotary Potentiometer (Small) [maximum_resistance=100kΩ package=THT]

nets:
  GND: LCD1.VSS, LCD1.R/W, LCD1.DB0, LCD1.DB1, LCD1.DB2, LCD1.DB3, Part1.D8, Part1.GND, HT9032D1.S, HT9032D1.GND, Q1.E, S1.leg1, R1.leg2
  VDD: LCD1.VDD, Part1.5V, HT9032D1.+, R3.Pin_0, R1.leg1
  N1: LCD1.V0, R1.wiper
  N2: LCD1.RS, Part1.D2
  N3: LCD1.E, Part1.D3_PWM
  N4: LCD1.DB4, Part1.D4
  N5: LCD1.DB5, Part1.D5_PWM
  N6: LCD1.DB6, Part1.D6_PWM
  N7: LCD1.DB7, Part1.D7
  N8: LCD1.LED+, R3.Pin_1
  N9: LCD1.LED-, Q1.C
  N10: Part1.A0, S1.leg0
  N11: Part1.D9_PWM, HT9032D1.P
  N12: Part1.D10_PWM/SS, HT9032D1.D
  N13: Part1.D12/MISO, R2.Pin_1
  N14: Q1.B, R2.Pin_0

notes:
  LCD Contrast
  50K
  2N3904
  16x2 HD44780 LCD Display
  Arduino Uno
  HT9032D Module
  Last Call
  Push Switch
  RED : +5V
  BLACK : GND

custom parts:
  HT9032D Calle ID Module: HT9032D Calle ID Module with Ring sense.
